# Fritzing sketch circuit_bluetooth_module (saved by Fritzing 0.9.5d)
breadboards: 1

parts:
  Componente1 = Arduino Mega 2560 (Rev3)
  R1 = Resistor [tolerance=±5% resistance=1k package="2010 [SMD]"]
  R2 = Resistor [tolerance=±5% resistance=1k package="2010 [SMD]"]
  R3 = Resistor [tolerance=±5% resistance=1k package="2010 [SMD]"]
  Componente2 = Bluetooth HC-05

nets:
  5V: Componente1.5V, Componente2.VCC
  GND: Componente1.GND, R1.Pin_0, Componente2.GND
  N1: Componente1.D2_PWM, Componente2.TXD
  N2: Componente1.D3_PWM, R3.Pin_1
  N3: R1.Pin_1, R2.Pin_0
  N4: R2.Pin_1, R3.Pin_0, Componente2.RXD
